// Logisim project lab4.circ as structural Verilog: 4 circuits, main circuit main
module main (
  input  w,
  input  x,
  input  y,
  input  z,
  output A___w___xz___xy,
  output out_6,
  output C___y_prime_z_prime___yz,
  output D___z_prime
);

  wire ic_7404_1_out_7, ic_7404_1_out_8, ic_7404_1_out_12, ic_7411_1_out_13, ic_7411_1_out_14,
       ic_7411_1_out_15, ic_7411_1_out_16, ic_7411_2_out_13, ic_7411_2_out_15, ic_7411_2_out_16;

  IC_7404 ic_7404_1 (
    .in_1(x), .in_2(y), .in_3(z), .in_6(ic_7411_2_out_15), .out_7(ic_7404_1_out_7), .out_8(ic_7404_1_out_8),
    .out_9(D___z_prime), .out_12(ic_7404_1_out_12));  // open: in_4, in_5, out_10, out_11
  IC_7411 ic_7411_1 (
    .in_1(x), .in_3(z), .out_13(ic_7411_1_out_13), .in_4(x), .in_5(y), .out_14(ic_7411_1_out_14),
    .in_7(ic_7404_1_out_7), .in_8(z), .out_15(ic_7411_1_out_15), .in_10(ic_7404_1_out_7), .in_11(y),
    .out_16(ic_7411_1_out_16));  // open: in_2, in_6, in_9, in_12
  IC_7411 ic_7411_2 (
    .in_1(x), .in_3(ic_7404_1_out_8), .out_13(ic_7411_2_out_13), .in_2(D___z_prime), .in_8(z),
    .out_15(ic_7411_2_out_15), .in_9(y), .in_10(y), .in_11(z), .out_16(ic_7411_2_out_16));  // open: in_4, in_5, out_14, in_6, in_7, in_12
  IC_4075 ic_4075_1 (
    .in_1(w), .in_2(ic_7411_1_out_14), .in_3(ic_7411_1_out_13), .out_10(A___w___xz___xy),
    .in_5(ic_7411_1_out_15), .out_11(out_6), .in_6(ic_7411_1_out_16), .in_4(ic_7411_2_out_13),
    .in_7(ic_7404_1_out_12), .in_8(ic_7411_2_out_16), .out_12(C___y_prime_z_prime___yz));  // open: in_9

  // Notes on the sheet:
  //   x'
  //   y'
  //   xz
  //   xy
  //   x'z
  //   x'y
  //   z'
  //   y'z'
  //   xy'z'
  //   yz
  //   B = x'z + x'y + xy'z'
endmodule

module IC_7411 (
  input  in_1,
  input  in_2,
  input  in_3,
  input  in_4,
  input  in_5,
  input  in_6,
  input  in_7,
  input  in_8,
  input  in_9,
  input  in_10,
  input  in_11,
  input  in_12,
  output out_13,
  output out_14,
  output out_15,
  output out_16
);

  and and_1 (out_13, in_1, in_2, in_3);
  and and_2 (out_14, in_4, in_5, in_6);
  and and_3 (out_15, in_7, in_8, in_9);
  and and_4 (out_16, in_10, in_11, in_12);
endmodule

module IC_7404 (
  input  in_1,
  input  in_2,
  input  in_3,
  input  in_4,
  input  in_5,
  input  in_6,
  output out_7,
  output out_8,
  output out_9,
  output out_10,
  output out_11,
  output out_12
);

  not not_1 (out_7, in_1);
  not not_2 (out_8, in_2);
  not not_3 (out_9, in_3);
  not not_4 (out_10, in_4);
  not not_5 (out_11, in_5);
  not not_6 (out_12, in_6);
endmodule

module IC_4075 (
  input  in_1,
  input  in_2,
  input  in_3,
  input  in_4,
  input  in_5,
  input  in_6,
  input  in_7,
  input  in_8,
  input  in_9,
  output out_10,
  output out_11,
  output out_12
);

  or or_1 (out_10, in_1, in_2, in_3);
  or or_2 (out_11, in_4, in_5, in_6);
  or or_3 (out_12, in_7, in_8, in_9);
endmodule
